# Fritzing sketch DRAW (saved by Fritzing 1.0.5)

parts:
  Mod1 = Amica NodeMCU DEVKIT 1.0
  M1 = MAX485 Breakout [package=THT]
  U1 = LM2596 step down module
  Arduino_CNC_Shield_V3_00_1 = Arduino_CNC_V3.00
  JL012-13-5_1 = JL012-13-5.2 Lever (Limit) Switch SPDT + NO + NC [part_number=JL012-13-5.2]
  JL012-13-5_2 = JL012-13-5.2 Lever (Limit) Switch SPDT + NO + NC [part_number=JL012-13-5.2]
  JL012-13-5_3 = JL012-13-5.2 Lever (Limit) Switch SPDT + NO + NC [part_number=JL012-13-5.2]
  JL012-13-5_4 = JL012-13-5.2 Lever (Limit) Switch SPDT + NO + NC [part_number=JL012-13-5.2]
  M2 = MAX485 Breakout [package=THT]
  U2 = LM2596 step down module
  J1 = Basic Servo
  8_Channel_Relay1 = 8 Channel Power Relay
  M3 = 1 chan 5v relay module
  M4 = MAX485 Breakout [package=THT]
  U3 = LM2596 step down module
  Arduino_CNC_Shield_V3_00_2 = Arduino_CNC_V3.00
  JL012-13-5_5 = JL012-13-5.2 Lever (Limit) Switch SPDT + NO + NC [part_number=JL012-13-5.2]
  JL012-13-5_6 = JL012-13-5.2 Lever (Limit) Switch SPDT + NO + NC [part_number=JL012-13-5.2]
  JL012-13-5_7 = JL012-13-5.2 Lever (Limit) Switch SPDT + NO + NC [part_number=JL012-13-5.2]
  J2 = Basic Servo
  JL012-13-5_8 = JL012-13-5.2 Lever (Limit) Switch SPDT + NO + NC [part_number=JL012-13-5.2]
  WATER_PUMP1 = water pump/motor  # not connected
  M5 = Getriebemotor  # not connected
  U4 = Vibration Motor- ROB-08449 [package=vibe-motor-10mm]
  S1 = Toggle Switch [package=THT]
  U5 = Vibration Motor- ROB-08449 [package=vibe-motor-10mm]
  S2 = Toggle Switch [package=THT]
  U6 = Vibration Motor- ROB-08449 [package=vibe-motor-10mm]
  S3 = Toggle Switch [package=THT]
  U7 = Vibration Motor- ROB-08449 [package=vibe-motor-10mm]
  S4 = Toggle Switch [package=THT]

nets:
  N1: Mod1.pin3, M1.DI
  N2: Mod1.pin4, M1.RO
  N3: Mod1.pin5, 8_Channel_Relay1.IN8
  N4: Mod1.pin6, 8_Channel_Relay1.IN7
  N5: Mod1.pin7, 8_Channel_Relay1.IN6
  N6: Mod1.pin8, 8_Channel_Relay1.IN5
  N7: Mod1.pin_10, Mod1.pin_26, M3.pin_5
  N8: Mod1.pin_11, 8_Channel_Relay1.IN4
  N9: Mod1.pin_12, M1.DE
  N10: Mod1.pin_13, M3.pin_4
  N11: Mod1.pin_14, 8_Channel_Relay1.IN3
  N12: Mod1.pin_15, 8_Channel_Relay1.IN1
  N13: U1.IN-, U1.OUT-, 8_Channel_Relay1.GND, M3.pin_2
  N14: U1.OUT+, 8_Channel_Relay1.VCC, M3.pin_1
  5V: Arduino_CNC_Shield_V3_00_1.5V, M2.VCC, U2.OUT+
  GND: Arduino_CNC_Shield_V3_00_1.GND, M2.GND, U2.IN-, U2.OUT-
  N15: Arduino_CNC_Shield_V3_00_1.RX, M2.DI
  N16: Arduino_CNC_Shield_V3_00_1.SCL_/_Probe, M2.RO
  N17: Arduino_CNC_Shield_V3_00_1.End_Stops_Z+_(Gnd), JL012-13-5_1.C, JL012-13-5_4.C
  N18: Arduino_CNC_Shield_V3_00_1.End_Stops_Z-_(and_Z+)_/_SpnEn, JL012-13-5_1.NO
  N19: Arduino_CNC_Shield_V3_00_1.End_Stops_Y-_(and_Y+), JL012-13-5_2.NO
  N20: Arduino_CNC_Shield_V3_00_1.End_Stops_X-_(and_X+), JL012-13-5_3.NO
  N21: Arduino_CNC_Shield_V3_00_1.SpnDir, M2.RE
  N22: Arduino_CNC_Shield_V3_00_1.CoolEn, JL012-13-5_4.NO
  N23: Arduino_CNC_Shield_V3_00_1.Resume, J1.pulse
  N24: 8_Channel_Relay1.NO#35, S2.L1
  N25: 8_Channel_Relay1.NO#41, S4.L1
  N26: 8_Channel_Relay1.NO#44, S1.L1
  N27: M4.RO, Arduino_CNC_Shield_V3_00_2.SCL_/_Probe
  N28: M4.RE, Arduino_CNC_Shield_V3_00_2.SpnDir
  N29: M4.DI, Arduino_CNC_Shield_V3_00_2.RX
  GND_2: M4.GND, U3.IN-, U3.OUT-, Arduino_CNC_Shield_V3_00_2.GND
  VCC: M4.VCC, U3.OUT+, Arduino_CNC_Shield_V3_00_2.5V
  N30: Arduino_CNC_Shield_V3_00_2.End_Stops_Z+_(Gnd), JL012-13-5_5.C, JL012-13-5_8.C
  N31: Arduino_CNC_Shield_V3_00_2.End_Stops_Z-_(and_Z+)_/_SpnEn, JL012-13-5_5.NO
  N32: Arduino_CNC_Shield_V3_00_2.End_Stops_Y-_(and_Y+), JL012-13-5_6.NO
  N33: Arduino_CNC_Shield_V3_00_2.End_Stops_X-_(and_X+), JL012-13-5_7.NO
  N34: Arduino_CNC_Shield_V3_00_2.CoolEn, JL012-13-5_8.NO
  N35: Arduino_CNC_Shield_V3_00_2.Resume, J2.pulse
  N36: U4.-, S1.COM
  N37: S1.L2, S4.L2
  N38: U5.-, S2.COM
  N39: U6.-, S3.COM
  N40: U7.-, S4.COM

custom parts:
  MAX485 Breakout: MAX485 RS485 breakout board
  LM2596 step down module: LM2596 DC-DC step down power supply module 3 A.
  Arduino_CNC_V3.00: Protoneer Arduino CNC Shield V3.00 If using Grbl V0.9: The “A” axis can not be used (yet). The “SCL” (Arduino A5) pin is now used for 'Probing' input. The “End Stops Z+ & Z-” (Arduino D11) and “SpnEn” (Arduino D12) have been switched!
  JL012-13-5.2 Lever (Limit) Switch SPDT + NO + NC: Micro Switch; Model No.: JL012-13.5-2; Actuator Action: Momentary; Actuator Type: Hinge Lever; Contact Configuration: 1NO, 1NC (SPDT) Temperature -25~65℃；Relative humidity: below 85%; Rate Voltage: 125V AC; Rated Current: 1A.
  8 Channel Power Relay: An 8 channel power relay. The module operates at 5V.
  1 chan 5v relay module: 1 Channel 5V Relay Module Board Shield with Optocoupler Support High and Low Level Trigger for Arduino.
  water pump/motor: WATER PUMP BY ARDUBLOCKTR
